# Fritzing sketch schematic2 (saved by Fritzing 0.9.9b)
breadboards: 1

parts:
  MEGA = Arduino Mega ADK (Rev3)
  A1 = prefix0000
  M1 = Stepper Motor - Bipolar
  JP2 = Header 5x2 [package=2x5-ra]
  U1 = LIPO-1000mAh [package=lipo-1000]
  YUMI_I/O = Header 1 [package=1x01_offset]
  U4 = Voltage Regulator [package=v-reg_dpack]

nets:
  N1: MEGA.A0, U4.OUT
  N2: MEGA.5V, A1.connector7, A1.connector9, A1.connector11
  N3: MEGA.D5_PWM, A1.connector10
  N4: MEGA.D6_PWM, A1.connector8
  N5: MEGA.D7_PWM, A1.connector6
  N6: A1.connector0, JP2.9
  N7: A1.connector1, JP2.7
  N8: A1.connector2, JP2.5
  N9: A1.connector3, JP2.3
  N10: A1.connector4, U1.+
  N11: A1.connector5, U1.-
  N12: M1.A, JP2.4
  N13: M1.C, JP2.6
  N14: M1.B, JP2.8
  N15: M1.D, JP2.10
  N16: YUMI_I/O.1, U4.ADJ, U4.IN
