# Fritzing sketch schematic3 (saved by Fritzing 0.9.9b)
breadboards: 1

parts:
  MEGA = Arduino Mega ADK (Rev3)
  A1 = prefix0000
  M1 = Stepper Motor - Bipolar
  JP2 = Header 5x2 [package=2x5-ra]
  U1 = LIPO-1000mAh [package=lipo-1000]
  YUMI_I/O = Header 1 [package=1x01_offset]
  DC1 = DC_DC_XL4016 [package=board_screw]

nets:
  N1: MEGA.A0, DC1.OUT+
  N2: MEGA.5V, A1.connector7, A1.connector9, A1.connector11
  N3: MEGA.D5_PWM, A1.connector10
  N4: MEGA.D6_PWM, A1.connector8
  N5: MEGA.D7_PWM, A1.connector6
  N6: MEGA.GND, DC1.OUT-
  N7: A1.connector0, JP2.9
  N8: A1.connector1, JP2.7
  N9: A1.connector2, JP2.5
  N10: A1.connector3, JP2.3
  N11: A1.connector4, U1.+
  N12: A1.connector5, U1.-, DC1.IN-
  N13: M1.A, JP2.4
  N14: M1.C, JP2.6
  N15: M1.B, JP2.8
  N16: M1.D, JP2.10
  N17: YUMI_I/O.1, DC1.IN+
